// Logisim project processor.circ as structural Verilog
module ALU (
  input  [2:0] F,
  input  [31:0] B,
  input  [31:0] A,
  input  [31:0] in_4,
  output [31:0] Y
);

  wire bitselector_1_out;
  wire [31:0] adder_1_out, and_1_out, multiplexer_1_out, not_1_out, or_1_out;

  Multiplexer #(.width(32), .enable("false")) multiplexer_1 (
    .in0(B), .in1(not_1_out), .out(multiplexer_1_out), .sel(F[2]));
  assign not_1_out = ~B;  // NOT_Gate not_1, 32 bits wide
  assign and_1_out = multiplexer_1_out & A;  // AND_Gate and_1, 32 bits wide
  assign or_1_out = multiplexer_1_out | A;  // OR_Gate or_1, 32 bits wide
  Adder #(.width(32)) adder_1 (.a(multiplexer_1_out), .b(A), .out(adder_1_out), .cin(F[2]));  // open: cout
  Multiplexer #(.select(2), .width(32), .enable("false")) multiplexer_2 (
    .in0(and_1_out), .in1(or_1_out), .in2(adder_1_out), .in3(in_4), .out(Y), .sel(F[1:0]));
  assign in_4 = {{31{1'b0}}, bitselector_1_out};  // Bit_Extender bit_extender_1
  BitSelector #(.width(32)) bitselector_1 (.in(adder_1_out), .out(bitselector_1_out), .sel({5{1'b1}}));
endmodule

module Datapath (
  input  [31:0] in_1,
  output [15:0] out_2,
  output [31:0] v0,
  output [2:0] A1,
  output [2:0] A2,
  output [7:0] out_6,
  output [31:0] V0_2
);

  wire ALUSrc, and_1_out, and_2_out, and_3_out, and_4_out, and_5_out, and_6_out, and_7_out, and_8_out,
       and_9_out, bitselector_9_out, Branch, Clock, comparator_1_eq, decoder_1_out0, decoder_1_out1,
       decoder_1_out2, decoder_1_out3, decoder_1_out4, decoder_1_out5, decoder_1_out6, decoder_1_out7,
       RegDst, RegWrite;
  wire [2:0] ALUControl, bitselector_4_out, multiplexer_2_out;
  wire [4:0] bitselector_5_out, bitselector_6_out;
  wire [7:0] adder_1_out, BTA, multiplexer_1_out, register_1_q, shifter_2_out;
  wire [15:0] Lower;
  wire [31:0] A, adder_3_out, and_10_out, B, multiplexer_4_out, multiplexer_6_out, not_1_out, or_1_out,
       register_2_q, register_3_q, register_5_q, register_6_q, register_7_q, register_8_q, register_9_q,
       rom_1_data, shifter_1_out, shifter_3_out, signext_imm, WD3;

  Comparator #(.width(32), .mode("unsigned")) comparator_1 (
    .a(WD3), .b({32{1'b0}}), .eq(comparator_1_eq));  // open: gt, lt
  and and_1 (and_1_out, comparator_1_eq, Branch);
  Multiplexer #(.width(8), .enable("false")) multiplexer_1 (
    .in0(adder_1_out), .in1(BTA), .out(multiplexer_1_out), .sel(and_1_out));
  Shifter #(.width(32)) shifter_1 (.in(signext_imm), .\dist (5'b00010), .out(shifter_1_out));
  Clock clock_1 (.out(Clock));
  Register register_1 (.D(multiplexer_1_out), .Q(register_1_q), .clk(Clock));  // open: en, clr
  BitSelector #(.width(32), .group(8)) bitselector_1 (.in(shifter_1_out), .out(out_6), .sel(2'b00));
  Shifter #(.shift("lr")) shifter_2 (.in(register_1_q), .\dist (3'b010), .out(shifter_2_out));
  Adder adder_1 (.a(register_1_q), .b(8'h4), .out(adder_1_out));  // open: cin, cout
  Adder adder_2 (.a(adder_1_out), .b(out_6), .out(BTA));  // open: cin, cout
  ROM #(.dataWidth(32)) rom_1 (.addr(shifter_2_out), .data(rom_1_data));  // open: sel
  BitSelector #(.width(32), .group(16)) bitselector_2 (.in(rom_1_data), .out(out_2), .sel(1'b1));
  BitSelector #(.width(32), .group(16)) bitselector_3 (.in(rom_1_data), .out(Lower), .sel(1'b0));
  Shifter #(.width(32), .shift("lr")) shifter_3 (.in(rom_1_data), .\dist (5'b01011), .out(shifter_3_out));
  ControlUnit controlunit_1 (
    .Instruction(rom_1_data), .RegDst(RegDst), .RegWrite(RegWrite), .ALUControl(ALUControl), .Branch(Branch),
    .ALUSrc(ALUSrc));
  BitSelector #(.width(32), .group(3)) bitselector_4 (.in(shifter_3_out), .out(bitselector_4_out), .sel(4'b0000));
  Decoder #(.select(3)) decoder_1 (
    .out0(decoder_1_out0), .out1(decoder_1_out1), .out2(decoder_1_out2), .out3(decoder_1_out3),
    .out4(decoder_1_out4), .out5(decoder_1_out5), .out6(decoder_1_out6), .out7(decoder_1_out7),
    .sel(multiplexer_2_out));  // open: en
  Multiplexer #(.width(3), .enable("false")) multiplexer_2 (
    .in0(A2), .in1(bitselector_4_out), .out(multiplexer_2_out), .sel(RegDst));
  and and_2 (and_2_out, RegWrite, decoder_1_out0);
  and and_3 (and_3_out, RegWrite, decoder_1_out1);
  and and_4 (and_4_out, RegWrite, decoder_1_out2);
  and and_5 (and_5_out, RegWrite, decoder_1_out3);
  and and_6 (and_6_out, RegWrite, decoder_1_out4);
  and and_7 (and_7_out, RegWrite, decoder_1_out5);
  and and_8 (and_8_out, RegWrite, decoder_1_out6);
  and and_9 (and_9_out, RegWrite, decoder_1_out7);
  BitSelector #(.width(16), .group(5)) bitselector_5 (.in(out_2), .out(bitselector_5_out), .sel(2'b01));
  BitSelector #(.width(16), .group(5)) bitselector_6 (.in(out_2), .out(bitselector_6_out), .sel(2'b00));
  Register #(.width(32)) register_2 (.D({32{1'b0}}), .en(and_2_out), .Q(register_2_q), .clk(Clock));  // open: clr
  Register #(.width(32)) register_3 (.D(WD3), .en(and_3_out), .Q(register_3_q), .clk(Clock));  // open: clr
  Register #(.width(32)) register_4 (.D(WD3), .en(and_4_out), .Q(V0_2), .clk(Clock));  // open: clr
  Register #(.width(32)) register_5 (.D(WD3), .en(and_5_out), .Q(register_5_q), .clk(Clock));  // open: clr
  Register #(.width(32)) register_6 (.D(WD3), .en(and_6_out), .Q(register_6_q), .clk(Clock));  // open: clr
  Register #(.width(32)) register_7 (.D(WD3), .en(and_7_out), .Q(register_7_q), .clk(Clock));  // open: clr
  Register #(.width(32)) register_8 (.D(WD3), .en(and_8_out), .Q(register_8_q), .clk(Clock));  // open: clr
  Register #(.width(32)) register_9 (.D(WD3), .en(and_9_out), .Q(register_9_q), .clk(Clock));  // open: clr
  BitSelector #(.width(5), .group(3)) bitselector_7 (.in(bitselector_5_out), .out(A1), .sel(1'b0));
  BitSelector #(.width(5), .group(3)) bitselector_8 (.in(bitselector_6_out), .out(A2), .sel(1'b0));
  Multiplexer #(.select(3), .width(32)) multiplexer_3 (
    .in0(register_2_q), .in1(register_3_q), .in2(V0_2), .in3(register_5_q), .in4(register_6_q),
    .in5(register_7_q), .in6(register_8_q), .in7(register_9_q), .out(A), .sel(A1));  // open: en
  Multiplexer #(.select(3), .width(32)) multiplexer_4 (
    .in0(register_2_q), .in1(register_3_q), .in2(V0_2), .in3(register_5_q), .in4(register_6_q),
    .in5(register_7_q), .in6(register_8_q), .in7(register_9_q), .out(multiplexer_4_out), .sel(A2));  // open: en
  assign signext_imm = {{16{Lower[15]}}, Lower};  // Bit_Extender bit_extender_1
  Multiplexer #(.width(32), .enable("false")) multiplexer_5 (
    .in0(multiplexer_4_out), .in1(signext_imm), .out(B), .sel(ALUSrc));
  Multiplexer #(.width(32), .enable("false")) multiplexer_6 (
    .in0(B), .in1(not_1_out), .out(multiplexer_6_out), .sel(ALUControl[2]));
  assign not_1_out = ~B;  // NOT_Gate not_1, 32 bits wide
  assign and_10_out = multiplexer_6_out & A;  // AND_Gate and_10, 32 bits wide
  assign or_1_out = multiplexer_6_out | A;  // OR_Gate or_1, 32 bits wide
  Adder #(.width(32)) adder_3 (.a(multiplexer_6_out), .b(A), .out(adder_3_out), .cin(ALUControl[2]));  // open: cout
  BitSelector #(.width(32)) bitselector_9 (.in(adder_3_out), .out(bitselector_9_out), .sel({5{1'b1}}));
  Multiplexer #(.select(2), .width(32), .enable("false")) multiplexer_7 (
    .in0(and_10_out), .in1(or_1_out), .in2(adder_3_out), .in3(in_1), .out(WD3), .sel(ALUControl[1:0]));
  assign in_1 = {{31{1'b0}}, bitselector_9_out};  // Bit_Extender bit_extender_2

  // Other names for the same wires on the sheet: rt[2:0] = A2; Upper[15:0] = out_2

  // Notes on the sheet:
  //   contents of rom_1 (hex, n*v repeats v):
  //   20040000 20020001 20050000 10a40009 20030000 20060000 10c20003 651820 20c60001 1000fffc 431020
  //   20a50001 1000fff6 1000ffff
endmodule

module Tests (
  output [31:0] Y,
  output [7:0] out_2,
  output [7:0] out_3,
  output [2:0] out_4
);

  BitSelector #(.width(32), .group(8)) bitselector_1 (.in(32'h12356789), .out(out_2), .sel(2'b01));
  BitSelector #(.width(32), .group(8)) bitselector_2 (.in(32'h12356789), .out(out_3), .sel(2'b01));
  BitSelector #(.group(3)) bitselector_3 (.in(out_3), .out(out_4), .sel(2'b00));

  assign Y = 32'hf4010207;

  // Notes on the sheet:
  //   binary values in Logisim. Convince yourself how the bits are displayed.
  //   Example 2: The bit selector is configured to have 32  
  //   bit group #1 (starting at index 0) is selected for the output.
  //   That is, the 8 bits 0x67 at bit indices 15..8  are sent to the output.
  //   Example 3: Now, assume that you want to extract 3 bits at   
  //   Example 1: A simple example that illustrates how 32-bit values are displayed as 
  //   input bits and 8 output bits. The parameter constant is 1, which means that   
  //   bit indices 10..8. This can be accoplished by putting two bit selecotrs in series.
endmodule

module RegisterFile (
  input  CLK,
  input  [2:0] A1,
  input  [31:0] WD3,
  input  [2:0] A2,
  input  WE3,
  input  [2:0] A3,
  output [31:0] RD1,
  output [31:0] RD2,
  output [31:0] V0
);

  wire and_1_out, and_2_out, and_3_out, and_4_out, and_5_out, and_6_out, and_7_out, and_8_out,
       decoder_1_out0, decoder_1_out1, decoder_1_out2, decoder_1_out3, decoder_1_out4, decoder_1_out5,
       decoder_1_out6, decoder_1_out7;
  wire [31:0] register_1_q, register_2_q, register_4_q, register_5_q, register_6_q, register_7_q,
       register_8_q;

  Decoder #(.select(3)) decoder_1 (
    .out0(decoder_1_out0), .out1(decoder_1_out1), .out2(decoder_1_out2), .out3(decoder_1_out3),
    .out4(decoder_1_out4), .out5(decoder_1_out5), .out6(decoder_1_out6), .out7(decoder_1_out7), .sel(A3));  // open: en
  and and_1 (and_1_out, WE3, decoder_1_out0);
  and and_2 (and_2_out, WE3, decoder_1_out1);
  and and_3 (and_3_out, WE3, decoder_1_out2);
  and and_4 (and_4_out, WE3, decoder_1_out3);
  and and_5 (and_5_out, WE3, decoder_1_out4);
  and and_6 (and_6_out, WE3, decoder_1_out5);
  and and_7 (and_7_out, WE3, decoder_1_out6);
  and and_8 (and_8_out, WE3, decoder_1_out7);
  Register #(.width(32)) register_1 (.D({32{1'b0}}), .en(and_1_out), .Q(register_1_q), .clk(CLK));  // open: clr
  Register #(.width(32)) register_2 (.D(WD3), .en(and_2_out), .Q(register_2_q), .clk(CLK));  // open: clr
  Register #(.width(32)) register_3 (.D(WD3), .en(and_3_out), .Q(V0), .clk(CLK));  // open: clr
  Register #(.width(32)) register_4 (.D(WD3), .en(and_4_out), .Q(register_4_q), .clk(CLK));  // open: clr
  Register #(.width(32)) register_5 (.D(WD3), .en(and_5_out), .Q(register_5_q), .clk(CLK));  // open: clr
  Register #(.width(32)) register_6 (.D(WD3), .en(and_6_out), .Q(register_6_q), .clk(CLK));  // open: clr
  Register #(.width(32)) register_7 (.D(WD3), .en(and_7_out), .Q(register_7_q), .clk(CLK));  // open: clr
  Register #(.width(32)) register_8 (.D(WD3), .en(and_8_out), .Q(register_8_q), .clk(CLK));  // open: clr
  Multiplexer #(.select(3), .width(32)) multiplexer_1 (
    .in0(register_1_q), .in1(register_2_q), .in2(V0), .in3(register_4_q), .in4(register_5_q),
    .in5(register_6_q), .in6(register_7_q), .in7(register_8_q), .out(RD1), .sel(A1));  // open: en
  Multiplexer #(.select(3), .width(32)) multiplexer_2 (
    .in0(register_1_q), .in1(register_2_q), .in2(V0), .in3(register_4_q), .in4(register_5_q),
    .in5(register_6_q), .in6(register_7_q), .in7(register_8_q), .out(RD2), .sel(A2));  // open: en
endmodule

module ControlUnit (
  input  [31:0] Instruction,
  output RegDst,
  output RegWrite,
  output ALUSrc,
  output [2:0] ALUControl,
  output Branch
);

  wire [5:0] bitselector_1_out;
  wire [31:0] shifter_1_out;

  Shifter #(.width(32), .shift("lr")) shifter_1 (.in(Instruction), .\dist (5'b11010), .out(shifter_1_out));
  BitSelector #(.width(32), .group(6)) bitselector_1 (.in(shifter_1_out), .out(bitselector_1_out), .sel(3'b000));
  Comparator #(.width(6), .mode("unsigned")) comparator_1 (
    .a(bitselector_1_out), .b(6'b001000), .eq(ALUSrc));  // open: gt, lt
  Comparator #(.width(6), .mode("unsigned")) comparator_2 (
    .a(bitselector_1_out), .b({6{1'b0}}), .eq(RegDst));  // open: gt, lt
  Comparator #(.width(6), .mode("unsigned")) comparator_3 (
    .a(bitselector_1_out), .b(6'b000100), .eq(Branch));  // open: gt, lt
  or or_1 (RegWrite, ALUSrc, RegDst);
  Multiplexer #(.width(3), .enable("false")) multiplexer_1 (.in0(3'b010), .in1(3'b110), .out(ALUControl), .sel(Branch));
endmodule
